// Logisim project Simple_CPU.circ as structural Verilog: 1 circuit, main circuit main
module main (
);

  wire button_1_out, clock_1_out, decoder_1_out0, decoder_1_out1, decoder_1_out3, or_1_out;
  wire [3:0] register_1_q, register_1_q_2;
  wire [7:0] adder_1_out, adder_2_out, multiplexer_1_out, ram_1_data, register_2_q, register_3_q;

  Clock clock_1 (.out(clock_1_out));
  Register register_1 (.D(ram_1_data), .en(1'b1), .clk(clock_1_out), .Q({register_1_q_2, register_1_q}));  // open: clr
  Register register_2 (.D(adder_1_out), .en(1'b1), .clk(clock_1_out), .Q(register_2_q), .clr(button_1_out));
  // Probe on ram_1_data
  Decoder #(.select(4)) decoder_1 (
    .out0(decoder_1_out0), .out1(decoder_1_out1), .out3(decoder_1_out3), .sel(register_1_q_2));  // open: out2, out4, out5, out6, out7, out8, out9, out10, out11, out12, out13, out14, out15, en
  // Probe on register_2_q
  // Probe on decoder_1_out0
  or or_1 (or_1_out, decoder_1_out1, decoder_1_out3);
  RAM #(.asyncread("true"), .databus("bidir")) ram_1 (
    .addr(register_2_q), .we(1'b0), .oe(1'b1), .clk(1'b1), .data(ram_1_data));
  Multiplexer #(.width(8)) multiplexer_1 (
    .in0(ram_1_data), .in1(adder_2_out), .out(multiplexer_1_out), .sel(decoder_1_out3));
  Register register_3 (.D(multiplexer_1_out), .en(or_1_out), .clk(clock_1_out), .Q(register_3_q));  // open: clr
  Adder adder_1 (.a(register_2_q), .b(8'h1), .out(adder_1_out));  // open: cin, cout
  Button button_1 (.out(button_1_out));
  Adder adder_2 (.a(register_3_q), .b(ram_1_data), .out(adder_2_out));  // open: cin, cout
  // Probe on ram_1_data
endmodule
